# Fritzing sketch schematics esp32 2xNema17 (saved by Fritzing 0.9.3b)

parts:
  Pololu_A4 = Pololu A4988 [package=SO16]
  Pololu_A5 = Pololu A4988 [package=SO16]
  M5 = Stepper Motor - Bipolar
  M6 = Stepper Motor - Bipolar
  U4 = LuaNode32 / ESP32 [part_number=ESP32S-PIN30]
  JACK2 = 2.1mm Barrel Jack with Terminal Block

nets:
  N1: Pololu_A4.MS1, Pololu_A4.MS2, Pololu_A4.MS3, U4.Vin
  N2: Pololu_A4.RESET, Pololu_A4.SLEEP
  N3: Pololu_A4.STEP, U4.D33
  N4: Pololu_A4.DIR, U4.D32
  N5: Pololu_A4.1B, M5.D
  N6: Pololu_A4.1A, M5.B
  N7: Pololu_A4.2A, M5.C
  N8: Pololu_A4.2B, M5.A
  N9: Pololu_A4.GND#14, Pololu_A5.GND#14, JACK2.NEG
  N10: Pololu_A4.VMOT, Pololu_A5.VMOT, JACK2.POS
  N11: Pololu_A5.MS1, Pololu_A5.MS2, Pololu_A5.MS3, Pololu_A5.VDD
  N12: Pololu_A5.RESET, Pololu_A5.SLEEP
  N13: Pololu_A5.STEP, U4.D26
  N14: Pololu_A5.DIR, U4.D25
  N15: Pololu_A5.1B, M6.D
  N16: Pololu_A5.1A, M6.B
  N17: Pololu_A5.2A, M6.C
  N18: Pololu_A5.2B, M6.A

custom parts:
  LuaNode32 / ESP32: New Image for LuaNode32 DOIT ESP32 DEVKIT V1. Base parts from LuaNode32 / ESP32 ESP32 based LuaNode32 by G.Noorlander DOIT Esp32 DevKit v1 (30 pins long, 11 pins width) by Werner Rothschopf (modified by vanepp Dec 2018)
